// Digital circuit main.dig as structural Verilog
module main (
  input  clk
);

  wire _7485_channels_1_p6, _7485_channels_1_p8, _7485_channels_1_p10, _74151_1_pin6, _74163_channels_1_p3,
       _74163_channels_1_p7, _74163_channels_2_p6, _74163_channels_3_p4, _74163_channels_4_p5,
       _74163_channels_6_p6, _74382_channels_1_p3, adr_src_sel, and_1_out, c_flag, eq_flag, gt_flag, inc_adr,
       \int , n_flag, nRST, nUJMP, o_flag, r_a, r_adr_h, r_adr_l, r_const, r_io, r_mem, r_y, st_flag, w_a,
       w_adr_h, w_adr_l, w_io, w_ir, w_mem, w_y;
  wire [2:0] alufunct, source_sel, target_sel;
  wire [3:0] _74163_channels_1_p4, _74163_channels_3_p5, \const , pulldown_3_out;
  wire [5:1] _74382_channels_2_p3;
  wire [7:0] _74382_channels_1_p1, a, databus, y;
  wire [7:6] d_ff_3_q;
  wire [11:0] ucode_adr;
  wire [15:0] adrreg, mem_adr, rom_1_d;

  Button button_1 (.out(\int ));
  Button #(.activeLow("true")) R (.out(nRST));
  _74138 _74138_1 (
    .pin1(target_sel[0]), .pin2(target_sel[1]), .pin3(target_sel[2]), .pin4(clk), .pin5(1'b0), .pin6(nUJMP),
    .pin8(1'b0), .pin9(w_io), .pin10(w_ir), .pin11(w_mem), .pin12(w_y), .pin13(w_a), .pin14(w_adr_l),
    .pin15(w_adr_h), .pin16(1'b1));  // open: pin7
  _74138 _74138_2 (
    .pin1(source_sel[0]), .pin2(source_sel[1]), .pin3(source_sel[2]), .pin4(1'b0), .pin5(1'b0), .pin6(1'b1),
    .pin8(1'b0), .pin9(r_io), .pin10(r_const), .pin11(r_mem), .pin12(r_y), .pin13(r_a), .pin14(r_adr_l),
    .pin15(r_adr_h), .pin16(1'b1));  // open: pin7
  ROM #(.bigEndian("true"), .AddrBits(12), .Bits(16)) rom_1 (.A(ucode_adr), .sel(1'b1), .D(rom_1_d));
  Delay #(.Bits(16), .delayTime(5)) delay_1 (
    .in(rom_1_d), .out({nUJMP, alufunct, \const , source_sel, target_sel, adr_src_sel, inc_adr}));
  and and_1 (and_1_out, nUJMP, inc_adr);
  // _74163_Channels _74163_channels_1: pin names not known; wires that end beside it: ucode_adr[3:0], nRST, _74163_channels_1_p3, _74163_channels_1_p4, 1'b1, 1'b1, _74163_channels_1_p7
  Multiplexer #(.Bits(4)) multiplexer_1 (
    .sel(nUJMP), .in_0({target_sel[1:0], adr_src_sel, inc_adr}), .in_1(databus[3:0]),
    .out(_74163_channels_1_p4));
  PullDown #(.Bits(8)) pulldown_1 (.out(databus));
  // _74163_Channels _74163_channels_2: pin names not known; wires that end beside it: clk, w_adr_l, 1'b1, and_1_out, databus[3:0], _74163_channels_2_p6, 1'b1, adrreg[3:0], clk
  // _74163_Channels _74163_channels_3: pin names not known; wires that end beside it: clk, ucode_adr[7:4], nRST, _74163_channels_3_p4, _74163_channels_3_p5, 1'b1, _74163_channels_1_p3, _74163_channels_1_p7
  Multiplexer #(.Bits(4)) multiplexer_2 (
    .sel(nUJMP), .in_0({source_sel, target_sel[2]}), .in_1(databus[7:4]), .out(_74163_channels_3_p5));
  // _74163_Channels _74163_channels_4: pin names not known; wires that end beside it: w_adr_l, _74163_channels_2_p6, and_1_out, databus[7:4], _74163_channels_4_p5, 1'b1, adrreg[7:4]
  Multiplexer #(.Bits(4)) multiplexer_3 (.sel(adr_src_sel), .in_0(adrreg[3:0]), .in_1(\const ), .out(mem_adr[3:0]));
  // _74163_Channels _74163_channels_5: pin names not known; wires that end beside it: clk, ucode_adr[11:8], nRST, \const , 1'b1, _74163_channels_3_p4, _74163_channels_1_p7, clk
  // _74163_Channels _74163_channels_6: pin names not known; wires that end beside it: clk, w_adr_h, _74163_channels_4_p5, and_1_out, databus[3:0], _74163_channels_6_p6, 1'b1, adrreg[11:8], clk
  assign mem_adr[9:4] = ~adr_src_sel ? adrreg[9:4] : 6'bz;  // DriverInvSel driverinvsel_1
  PullDown #(.Bits(16)) pulldown_2 (.out(mem_adr));
  // Probe on ucode_adr
  // Probe on adrreg
  // Probe on \const 
  and and_2 (_74163_channels_1_p7, w_ir, _74151_1_pin6);
  assign mem_adr[15:10] = ~adr_src_sel ? adrreg[15:10] : 6'bz;  // DriverInvSel driverinvsel_2
  // _74163_Channels _74163_channels_7: pin names not known; wires that end beside it: w_adr_h, _74163_channels_6_p6, and_1_out, databus[7:4], 1'b1, adrreg[15:12]
  RAMSinglePortSel #(.AddrBits(16), .isProgramMemory("true"), .Bits(8)) ramsingleportsel_1 (
    .A(mem_adr), .CS(~1'b0), .WE(~w_mem), .OE(~r_mem), .D(databus));
  _74151 _74151_1 (
    .pin1(o_flag), .pin2(c_flag), .pin3(n_flag), .pin4(1'b1), .pin6(_74151_1_pin6), .pin7(nUJMP),
    .pin8(1'b0), .pin9(alufunct[2]), .pin10(alufunct[1]), .pin11(alufunct[0]), .pin12(\int ),
    .pin13(eq_flag), .pin14(st_flag), .pin15(gt_flag), .pin16(1'b1));  // open: pin5
  PullDown #(.Bits(4)) pulldown_3 (.out(pulldown_3_out));
  // Probe on y
  // Probe on a
  // Probe on mem_adr
  // Probe on databus
  assign databus = ~r_adr_h ? adrreg[15:8] : 8'bz;  // DriverInvSel driverinvsel_3
  assign databus = ~r_adr_l ? adrreg[7:0] : 8'bz;  // DriverInvSel driverinvsel_4
  assign databus = ~r_const ? {pulldown_3_out, \const } : 8'bz;  // DriverInvSel driverinvsel_5
  assign databus = ~r_y ? y : 8'bz;  // DriverInvSel driverinvsel_6
  D_FF #(.Bits(8)) d_ff_1 (.D(_74382_channels_1_p1), .C(w_y), .Q(y));  // open: nQ
  assign databus = ~r_a ? a : 8'bz;  // DriverInvSel driverinvsel_7
  // _74382_Channels _74382_channels_1: pin names not known; wires that end beside it: _74382_channels_1_p1[3:0], a[3:0], _74382_channels_1_p3, databus[3:0], alufunct, 1'b0
  D_FF #(.Bits(8)) d_ff_2 (.D(databus), .C(w_a), .Q(a));  // open: nQ
  D_FF #(.Bits(8)) d_ff_3 (
    .D({2'b00, _74382_channels_2_p3, _74382_channels_1_p1[3]}), .C(w_y),
    .Q({d_ff_3_q, eq_flag, st_flag, gt_flag, o_flag, c_flag, n_flag}));  // open: nQ
  // _74382_Channels _74382_channels_2: pin names not known; wires that end beside it: _74382_channels_1_p1[7:4], a[7:4], _74382_channels_2_p3[1], databus[7:4], _74382_channels_2_p3[2], alufunct, _74382_channels_1_p3
  // _7485_Channels _7485_channels_1: pin names not known; wires that end beside it: _74382_channels_2_p3[3], a[7:4], _74382_channels_2_p3[4], databus[7:4], _74382_channels_2_p3[5], _7485_channels_1_p6, _7485_channels_1_p6, _7485_channels_1_p8, _7485_channels_1_p8, _7485_channels_1_p10, _7485_channels_1_p10
  // _7485_Channels _7485_channels_2: pin names not known; wires that end beside it: a[3:0], databus[3:0], 1'b0, 1'b1, 1'b0

  // Other names for the same wires on the sheet: JCOND[2:0] = alufunct

  // Notes on the sheet:
  //   rom_1 loads ucode.bin
endmodule
